# Fritzing sketch finalproj (saved by Fritzing 0.9.10b)

parts:
  Water_Level_Sensor1 = Water Level Sensor
  Part1 = Arduino Mega ADK (Rev3)
  7_Segment1 = 7 Segment Display
  YL-83_-_Detection_Board1 = YL-83 Rain Sensor - Detection Board
  YL-83_-_Control_Board1 = YL-83 Rain Sensor - Control Board
  J1 = Basic Servo
  Part2 = Arduino Uno (Rev3)
  Front1 = HC-SR04 Ultrasonic Distance Sensor
  backRight1 = HC-SR04 Ultrasonic Distance Sensor
  back_sensor1 = HC-SR04 Ultrasonic Distance Sensor
  J2 = Piezo Speaker
  L298N2 = L298N DC motor driver
  M5 = DC Motor [voltage_(max)=6V voltage_(min)=3V]
  M6 = DC Motor [voltage_(max)=6V voltage_(min)=3V]
  M7 = DC Motor [voltage_(max)=6V voltage_(min)=3V]
  M8 = DC Motor [voltage_(max)=6V voltage_(min)=3V]

nets:
  N1: Water_Level_Sensor1.SIG, Part1.A15
  GND: Water_Level_Sensor1.GND, Part1.GND, 7_Segment1.common_cathode
  N2: Part1.D19/RX1, Part2.D1/TX
  N3: Part1.D18/TX1, Part2.D0/RX
  VCC: Part1.5V, YL-83_-_Control_Board1.VCC, J1.vcc
  N4: Part1.D37, J1.pulse
  N5: Part1.D39, YL-83_-_Control_Board1.DO
  N6: Part1.D41, 7_Segment1.Segment_G
  N7: Part1.D43, 7_Segment1.Segment_F
  N8: Part1.D45, 7_Segment1.Segment_A
  N9: Part1.D47, 7_Segment1.Segment_B
  N10: Part1.D49, 7_Segment1.Segment_C
  N11: Part1.D51/MOSI, 7_Segment1.Segment_D
  N12: Part1.D53/SS, 7_Segment1.Segment_E
  N13: YL-83_-_Detection_Board1.POS, YL-83_-_Control_Board1.POS
  N14: YL-83_-_Detection_Board1.NEG, YL-83_-_Control_Board1.NEG
  N15: Part2.A5/SCL, J2.pin2
  N16: Part2.D8, Front1.TRIG
  N17: Part2.D9_PWM, Front1.ECHO
  N18: Part2.D10_PWM/SS, backRight1.ECHO
  N19: Part2.D11_PWM/MOSI, backRight1.TRIG
  N20: Part2.D12/MISO, back_sensor1.ECHO
  N21: Part2.D13/SCK, back_sensor1.TRIG
  GND_2: Part2.GND, Front1.GND, backRight1.GND, back_sensor1.GND, J2.pin1, L298N2.GND
  N22: Part2.D2, L298N2.ENB
  N23: Part2.D3_PWM, L298N2.IN4
  N24: Part2.D4, L298N2.IN3
  N25: Part2.D5_PWM, L298N2.IN2
  N26: Part2.D6_PWM, L298N2.IN1
  N27: Part2.D7, L298N2.ENA
  VCC_2: Part2.5V, Front1.VCC, backRight1.VCC, back_sensor1.VCC
  N28: L298N2.OUT1, M5.pin_2
  N29: L298N2.OUT2, M5.pin_1, M6.pin_1
  N30: L298N2.OUT3, M7.pin_2, M8.pin_2
  N31: L298N2.OUT4, M7.pin_1, M8.pin_1

notes:
  TEA5676
  SDA SCL
  [ 2.4 TFT LCD]
  D0 -> 22
  D1 ->23
  D2 ->24
  D3 ->25
  D4->26
  D5 ->27
  D6 ->28
  D7 ->29
  [2.4 TFT LCD]
  LCD_CS -----> A3
  LCD_CD------> A2
  LCD_WR-----> A1
  LCD_RD -----> A0
  LCD_RESET -> A4

custom parts:
  Water Level Sensor: A water level sensor. This sensor operates at 3V to 5V. The Sig (signal) pin outputs an analogue signal that is in proportion to the amount of water in contact with the sensor.
  YL-83 Rain Sensor - Detection Board: The YL-83 is a rain sensor that has more resistance when dry and less resistance when wet. The module runs at 5V.
  YL-83 Rain Sensor - Control Board: The YL-83 is a rain sensor that has more resistance when dry and less resistance when wet. The module runs at 5V.
  L298N DC motor driver: 2x DC motor driver with 78M05 positive voltage regulator (7..35 V) L298N: max 46 V, 2 A Set 5 V Enable jumper to enable 5 V regultor (needed for the L298N) and +5 V output at screw terminal or supply external +5 V at screw terminal Set ENA and/or ENB to +5 V to enable motor permanently or supply ENA and/or ENB with PWM signal IN1 and IN2 set rotation directory for motor A (OUT1/OUT2) IN2 and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
